# Fritzing sketch ChirpKitSchematic (saved by Fritzing 0.9.3b)

parts:
  SCK_1_1 = Smart Citizen Kit 1.5
  Chirp!_Soil_Moisture_Sensor1 = Chirp! Soil Moisture Sensor v2.7.3

nets:
  N1: SCK_1_1.GND, Chirp!_Soil_Moisture_Sensor1.pin_5
  N2: SCK_1_1.VCC, Chirp!_Soil_Moisture_Sensor1.Pin_1
  N3: SCK_1_1.SDA, Chirp!_Soil_Moisture_Sensor1.pin_3
  N4: SCK_1_1.SCL, Chirp!_Soil_Moisture_Sensor1.pin_2

custom parts:
  Smart Citizen Kit 1.5: Smart Citizen Kit 1.5 rev C
