# Fritzing sketch TensiometerKitSchematic (saved by Fritzing 0.9.3b)
stripboards: 1

parts:
  J1 = double row male pin header, 8 pins [form="♂ (male)"]
  J2 = male pin header, 1 pin [form="♂ (male)"]
  J3 = male pin header, 1 pin [form="♂ (male)"]
  R1 = Resistor [tolerance=±5% resistance=4.7k package=THT]
  R2 = Resistor [tolerance=±5% resistance=4.7k package=THT]
  D1 = Rectifier Diode [part_number=1N4148 breakdown_voltage=3.6V package="300 mil [THT]"]
  D2 = Rectifier Diode [part_number=1N4148 breakdown_voltage=3.6V package="300 mil [THT]"]
  J8 = Screw terminal - 2 pins [package=THT]

nets:
  N1: J1.pin1, J2.pin1
  N2: J1.pin2, R2.Pin_0, D1.cathode, J8.pin1
  N3: J1.pin3, R1.Pin_0, D2.cathode, J8.pin2
  N4: J1.pin6, D1.anode
  N5: J1.pin7, D2.anode
  N6: J1.pin8, J3.pin1, R1.Pin_1, R2.Pin_1
